# Fritzing sketch drawing (saved by Fritzing 0.9.3b)
breadboards: 1

parts:
  Part1 = Arduino Nano (Rev3.0)
  S1 = Square Pushbutton
  C1 = Capacitor Polarized [part_number=470uF package=nippon_f80]
  R1 = Resistor [tolerance=±5% resistance=470 package=THT]
  LED1 = smd LED [color="Red (633nm)" package="0603 [SMD]"]
  RGB_SMD_LED2 = SMD RGB LED (WS2812) [package=5050]
  R2 = Resistor [tolerance=±5% resistance=330 package=THT]
  R3 = Resistor [tolerance=±5% resistance=1k package=THT]
  Q1 = NPN-Transistor [package="TO92 [THT]"]

nets:
  GND: Part1.GND, S1.leg0, C1.-, Q1.E
  N1: Part1.D2, R1.Pin_0
  N2: Part1.D3, R2.Pin_0
  N3: Part1.D9, S1.leg1
  5V: Part1.5V, C1.+, RGB_SMD_LED2.VCC, RGB_SMD_LED2.VDD, R3.Pin_0
  N4: Part1.D13/SCK, LED1.cathode
  N5: R1.Pin_1, RGB_SMD_LED2.DIn
  N6: LED1.anode, R3.Pin_1
  N7: RGB_SMD_LED2.VSS, Q1.C
  N8: R2.Pin_1, Q1.B

notes:
  Supply +5V
  Supply GND
  Push Button
  LED ON/OFF
  Digital LED Control
